# Fritzing sketch Watch Winder Schematics (saved by Fritzing 0.9.3b)
breadboards: 1

parts:
  Part1 = Arduino Uno (Rev3)
  Part2 = Real Time Clock Module - DS1307 RTC Breakout Board  # not connected
  M1 = Stepper Motor - Bipolar
  DRV_1 = Pololu A4988 [package=SO16]
  I2C = PCF8575C [part_number="PCF2584 LED backpack" package=so-24dw]
  C1 = Electrolytic Capacitor [capacitance=47µF voltage=16V package="100 mil [THT, electrolytic]"]
  R1 = Resistor [tolerance=±5% resistance=10k package=THT]
  R2 = Resistor [tolerance=±5% resistance=10k package=THT]
  S2 = Pushbutton [package="[SMD]"]
  S3 = Pushbutton [package="[SMD]"]
  S4 = Pushbutton [package="[SMD]"]
  S5 = Pushbutton [package="[SMD]"]
  S6 = Round Pushbutton
  R3 = Resistor [tolerance=±5% resistance=10k package=THT]

nets:
  N1: Part1.D8, Part1.D9_PWM, Part1.D5_PWM, Part1.D6_PWM, Part1.D7, S2.Pin_4, S4.Pin_3, S4.Pin_4, S5.Pin_4, S6.leg0, R3.Pin_0
  N2: Part1.A4/SDA, I2C.SDA
  N3: Part1.A5/SCL, I2C.SCL
  N4: Part1.D2, DRV_1.STEP
  N5: Part1.D3_PWM, DRV_1.DIR
  N6: Part1.D4, DRV_1.ENABLE
  N7: Part1.ioref, DRV_1.VDD
  5V: Part1.5V, I2C.VCC, R1.Pin_1, R2.Pin_1, S2.Pin_1, S2.Pin_2, S3.Pin_2, S4.Pin_2, S5.Pin_1, S5.Pin_2, S6.leg1
  GND: Part1.GND, DRV_1.GND, I2C.GND, C1.-, R3.Pin_1
  N8: Part1.VIN, DRV_1.VMOT
  N9: M1.A, DRV_1.2B
  N10: M1.C, DRV_1.2A
  N11: M1.B, DRV_1.1A
  N12: M1.D, DRV_1.1B
  N13: DRV_1.MS1, R1.Pin_0
  N14: DRV_1.MS2, R2.Pin_0
